# Fritzing sketch ESP8266_To_Upload (saved by Fritzing 0.9.3b)
breadboards: 1

parts:
  U1 = ESP8266 WiFi Module [part_number=ESP8266]
  S1 = Pushbutton [package="[THT]"]
  BAT3 = Battery Holders [package=battery]
  Part3 = FTDI Basic Programmer

nets:
  N1: U1.RXD, Part3.TXO
  N2: U1.VCC, BAT3.+
  N3: U1.CH_PD, S1.Pin_1, S1.Pin_2
  GND: U1.GND, S1.Pin_3, S1.Pin_4, BAT3.-, Part3.GND
  N4: U1.TXD, Part3.RXI

custom parts:
  ESP8266 WiFi Module: Generic WiFi Module based on the ESP8266 with onboard PCB antenna and UART communications
